# Fritzing sketch Wiring plan (saved by Fritzing 0.9.4)
breadboards: 1

parts:
  ESP1 = ESP 12E
  Q1 = TRANSISTOR_NPN [package=to-92]
  U1 = V_REG_LD1117VXX [package=78xxl]
  J1 = Camdenboss CTB0158-2 [part_number=CTB0158-2 package=THT]
  LED2 = LEDs [package=led10mm]
  S1 = Pushbutton [package="[SMD]"]
  R1 = Resistor [tolerance=±5% resistance=4.7k package="2010 [SMD]"]

nets:
  N1: ESP1.GPIO5, S1.Pin_3, S1.Pin_4, R1.Pin_1
  N2: ESP1.GPIO4, Q1.B
  GND: ESP1.GPIO15, ESP1.GND, Q1.C, U1.GND, J1.pin2, S1.Pin_1, S1.Pin_2
  N3: ESP1.VCC, ESP1.EN, U1.OUT, LED2.A, R1.Pin_0
  N4: Q1.E, LED2.C
  N5: U1.IN, J1.pin1

custom parts:
  ESP 12E: ESP 12e module with spi interface and wifi connection
